# Fritzing sketch Генератор псевдослучайных чисел fritzing (saved by Fritzing 0.9.3b)
breadboards: 1

parts:
  Часть1 = Arduino Uno (Rev3)
  L1 = Solenoid
  U1 = TCM8240MD [package=tcm8240md]  # not connected
  Raspberry_Pi1 = Raspberry Pi B+  # not connected
  VCC1 = Battery block 9V
  L7 = Solenoid
  L3 = Solenoid
  Driver1 = 28BYJ-48 Driver Module [part_number=ULN2003 package=THT]
  SM1 = 28BYJ-48 Stepper Motor [part_number=28BYJ-48]
  Driver2 = 28BYJ-48 Driver Module [part_number=ULN2003 package=THT]
  SM2 = 28BYJ-48 Stepper Motor [part_number=28BYJ-48]

nets:
  N1: Часть1.D8, Driver2.IN4
  N2: Часть1.D9_PWM, Driver2.IN3
  N3: Часть1.D10_PWM/SS, L1.pin2
  N4: Часть1.D11_PWM/MOSI, Driver2.IN2
  N5: Часть1.D12/MISO, Driver2.IN1
  N6: Часть1.D13/SCK, L7.pin2
  GND: Часть1.GND, L1.pin1, VCC1.-, L7.pin1, L3.pin1, Driver1.GND, Driver2.GND
  N7: Часть1.D2, Driver1.IN4
  N8: Часть1.D3_PWM, Driver1.IN3
  N9: Часть1.D4, Driver1.IN2
  N10: Часть1.D5_PWM, Driver1.IN1
  N11: Часть1.D7, L3.pin2
  N12: Часть1.VIN, VCC1.+
  N13: Driver1.Vmotor, Driver2.Vmotor
  N14: Driver1.blue-pin, SM1.blue-pin
  N15: Driver1.pink-pin, SM1.pink-pin
  N16: Driver1.yellow-pin, SM1.yellow-pin
  N17: Driver1.orange-pin, SM1.orange-pin
  N18: Driver1.red-pin, SM1.red-pin
  N19: Driver2.blue-pin, SM2.blue-pin
  N20: Driver2.pink-pin, SM2.pink-pin
  N21: Driver2.yellow-pin, SM2.yellow-pin
  N22: Driver2.orange-pin, SM2.orange-pin
  N23: Driver2.red-pin, SM2.red-pin

custom parts:
  28BYJ-48 Driver Module: ULN2003 Driver Module for the 28BYJ-48 Unipolar Stepper Motor LED A - Blue wire - Bottom coil left LED B - Pink wire - Top coil left LED C - Yellow wire - Bottom coil right LED D - Orange wire - Top coil right Common rail - red Connector pins: blue - pink - yellow - orange - red Control pins - IN1 to IN4 Power pins - GND & Vmotor (5-12V) On/Off jumper (if removed, power to motor is cut).
  28BYJ-48 Stepper Motor: Unipolar Stepper Motor 28BYJ-48 Top coil - pink & orange Bottom coil - blue & yellow Common rail - red Connector pins: blue - pink - yellow - orange - red
